# Fritzing sketch termometro pt1000 (saved by Fritzing 0.9.3b)
breadboards: 1

parts:
  Componente1 = Arduino Uno (Rev3)
  R1 = Resistor [tolerance=±5% resistance=1k package=THT]
  R3 = 120 Ω Resistor [package=THT]  # not connected

nets:
  N1: Componente1.A1, R1.Pin_1
  N2: Componente1.5V, R1.Pin_0

custom parts:
  120 Ω Resistor: A generic resistor (0.25W)
